# Fritzing sketch transmitterside-project (saved by Fritzing 0.8.7b)
breadboards: 1

parts:
  BeagleBone1 = BeagleBone Black
  U1 = XBee
  U3 = Nokia 6100 Color LCD [package=nokia6100_lcd]

nets:
  N1: BeagleBone1.no_name_yet#1, U1.GND
  N2: BeagleBone1.no_name_yet#2, U3.CS
  N3: BeagleBone1.no_name_yet#4, U1.VCC
  N4: BeagleBone1.no_name_yet#5, U3.VDIGITAL
  N5: BeagleBone1.no_name_yet#21, U3.SCK
  N6: BeagleBone1.no_name_yet#22, U3.DIO
  N7: BeagleBone1.no_name_yet#24, U1.pin3
  N8: BeagleBone1.no_name_yet#26, U1.pin2

notes:
  Nextion
  NX4832T035_011R
  display 3,5"

custom parts:
  BeagleBone Black: BeagleBone Black rev. A5B
